// Logisim project full-adder.circ as structural Verilog: 1 circuit, main circuit main
module main (
  input  A,
  input  B,
  input  C,
  output S,
  output C_2
);

  wire and_1_out, and_2_out, and_3_out, and_4_out, and_5_out, and_6_out, and_7_out, not_1_out, not_2_out,
       not_3_out;

  not not_1 (not_1_out, A);
  not not_2 (not_2_out, B);
  not not_3 (not_3_out, C);
  and and_1 (and_1_out, not_1_out, not_2_out, C);
  and and_2 (and_2_out, not_1_out, not_3_out, B);
  and and_3 (and_3_out, A, B, C);
  and and_4 (and_4_out, A, not_2_out, not_3_out);
  and and_5 (and_5_out, A, B);
  and and_6 (and_6_out, A, C);
  and and_7 (and_7_out, B, C);
  or or_1 (S, and_1_out, and_2_out, and_3_out, and_4_out);
  or or_2 (C_2, and_5_out, and_6_out, and_7_out);
endmodule
