// Logisim project COUNTER.circ as structural Verilog: 1 circuit, main circuit main
module main (
  input  in_1,
  output out_2,
  output out_3,
  output out_4
);

  wire and_1_out, and_2_out, and_3_out, and_4_out, and_5_out, and_6_out, and_7_out, and_8_out, and_9_out,
       clock_1_out, d_ff_1_q, d_ff_1_qn, d_ff_2_q, d_ff_2_qn, d_ff_3_q, d_ff_3_qn, not_1_out;

  Clock clock_1 (.out(clock_1_out));
  D_Flip_Flop d_ff_1 (.clk(clock_1_out), .D(out_2), .Q(d_ff_1_q), .Qn(d_ff_1_qn));  // open: preset, en, reset
  D_Flip_Flop d_ff_2 (.clk(clock_1_out), .D(out_3), .Q(d_ff_2_q), .Qn(d_ff_2_qn));  // open: preset, en, reset
  D_Flip_Flop d_ff_3 (.clk(clock_1_out), .D(out_4), .Q(d_ff_3_q), .Qn(d_ff_3_qn));  // open: preset, en, reset
  not not_1 (not_1_out, in_1);
  and and_1 (and_1_out, d_ff_1_q, d_ff_2_qn, d_ff_3_qn);
  and and_2 (and_2_out, in_1, d_ff_1_qn, d_ff_3_q);
  and and_3 (and_3_out, in_1, d_ff_1_qn, d_ff_2_q);
  and and_4 (and_4_out, not_1_out, d_ff_1_q);
  and and_5 (and_5_out, in_1, d_ff_2_qn, d_ff_3_qn);
  and and_6 (and_6_out, d_ff_2_q, d_ff_2_q, d_ff_3_q);
  and and_7 (and_7_out, not_1_out, d_ff_2_q);
  and and_8 (and_8_out, not_1_out, d_ff_3_q);
  and and_9 (and_9_out, in_1, d_ff_3_qn);
  or or_1 (out_2, and_1_out, and_2_out, and_3_out, and_4_out);
  or or_2 (out_3, and_5_out, and_6_out, and_7_out);
  or or_3 (out_4, and_8_out, and_9_out);
  Hex_Digit_Display hex_digit_display_1 (.value({1'b0, out_2, out_3, out_4}));  // open: dp

  // Notes on the sheet:
  //   GO
  //   S2
  //   S1
  //   S0
  //   NS2
  //   NS1
  //   NS0
endmodule
